# Fritzing sketch 7DigitDisplay (saved by Fritzing 0.9.2b)
breadboards: 1

parts:
  Raspberry_Pi2 = Raspberry Pi 2
  U3 = 7-SEGMENT-4DIGIT [part_number=FJ-5461BH package=7-segment-4digit]
  R3 = Resistor [tolerance=±5% resistance=390 package=THT]
  R4 = Resistor [tolerance=±5% resistance=390 package=THT]
  R5 = Resistor [tolerance=±5% resistance=390 package=THT]
  R6 = Resistor [tolerance=±5% resistance=390 package=THT]
  R7 = Resistor [tolerance=±5% resistance=390 package=THT]
  R8 = Resistor [tolerance=±5% resistance=390 package=THT]
  R9 = Resistor [tolerance=±5% resistance=390 package=THT]
  R10 = Resistor [tolerance=±5% resistance=390 package=THT]

nets:
  N1: Raspberry_Pi2.GPIO27, U3.pin12
  N2: Raspberry_Pi2.GPIO22, U3.pin9
  N3: Raspberry_Pi2.GPIO5, U3.pin8
  N4: Raspberry_Pi2.GPIO6, R4.Pin_0
  N5: Raspberry_Pi2.GPIO13, R3.Pin_0
  N6: Raspberry_Pi2.GPIO26, U3.pin6
  N7: Raspberry_Pi2.GPIO16, R5.Pin_0
  N8: Raspberry_Pi2.GPIO12, R6.Pin_0
  N9: Raspberry_Pi2.GPIO25, R7.Pin_0
  N10: Raspberry_Pi2.GPIO24, R10.Pin_0
  N11: Raspberry_Pi2.GPIO23, R9.Pin_0
  N12: Raspberry_Pi2.GPIO18, R8.Pin_0
  N13: U3.pin1, R8.Pin_1
  N14: U3.pin2, R9.Pin_1
  N15: U3.pin3, R10.Pin_1
  N16: U3.pin4, R7.Pin_1
  N17: U3.pin5, R6.Pin_1
  N18: U3.pin7, R3.Pin_1
  N19: U3.pin10, R4.Pin_1
  N20: U3.pin11, R5.Pin_1
