# Fritzing sketch LightDiode (saved by Fritzing 0.9.2b)
breadboards: 1

parts:
  LED1 = LED - 5mm [color="Blue (430nm)" package="5 mm [THT]"]
  LED2 = LED - 5mm [color="Red (633nm)" package="5 mm [THT]"]
  LED3 = LED - 5mm [color="Yellow (595nm)" package="5 mm [THT]"]
  LED4 = LED - 5mm [color="Green (555nm)" package="5 mm [THT]"]
  Raspberry_Pi1 = Raspberry Pi 2
  R1 = Resistor [tolerance=±5% resistance=330 package=THT]
  R2 = Resistor [tolerance=±5% resistance=330 package=THT]
  R3 = Resistor [tolerance=±5% resistance=330 package=THT]
  R4 = Resistor [tolerance=±5% resistance=330 package=THT]

nets:
  N1: LED1.cathode, R3.Pin_0
  N2: LED1.anode, LED2.anode, LED3.anode, LED4.anode, Raspberry_Pi1.GPIO4
  N3: LED2.cathode, R1.Pin_0
  N4: LED3.cathode, R4.Pin_0
  N5: LED4.cathode, R2.Pin_0
  N6: Raspberry_Pi1.GND, R1.Pin_1, R2.Pin_1, R3.Pin_1, R4.Pin_1
